# Fritzing sketch Untitled Sketch (saved by Fritzing 0.7.4b)
breadboards: 1

parts:
  Arduino1 = Arduino
  part = Resistor [tolerance=±5% resistance=100 package=THT]
  part_2 = Resistor [tolerance=±5% resistance=100 package=THT]
  part_3 = Resistor [tolerance=±5% resistance=100 package=THT]
  part_4 = Resistor [tolerance=±5% resistance=100 package=THT]
  part_5 = Resistor [tolerance=±5% resistance=100 package=THT]
  part_6 = Resistor [tolerance=±5% resistance=100 package=THT]
  part_7 = Resistor [tolerance=±5% resistance=100 package=THT]
  part_8 = Resistor [tolerance=±5% resistance=100 package=THT]
  part_9 = Resistor [tolerance=±5% resistance=100 package=THT]
  part_10 = Resistor [tolerance=±5% resistance=100 package=THT]
  part_11 = Resistor [tolerance=±5% resistance=100 package=THT]
  part_12 = LED - 5mm [color="Red (633nm)" package="5 mm [THT]"]
  LED2 = LED - 5mm [color="Red (633nm)" package="5 mm [THT]"]
  LED3 = LED - 5mm [color="Red (633nm)" package="5 mm [THT]"]
  LED4 = LED - 5mm [color="Red (633nm)" package="5 mm [THT]"]
  LED5 = LED - 5mm [color="Red (633nm)" package="5 mm [THT]"]
  LED6 = LED - 5mm [color="Red (633nm)" package="5 mm [THT]"]
  LED7 = LED - 5mm [color="Red (633nm)" package="5 mm [THT]"]
  LED8 = LED - 5mm [color="Red (633nm)" package="5 mm [THT]"]
  LED9 = LED - 5mm [color="Red (633nm)" package="5 mm [THT]"]
  LED10 = LED - 5mm [color="Red (633nm)" package="5 mm [THT]"]
  LED11 = LED - 5mm [color="Red (633nm)" package="5 mm [THT]"]
  part_13 = LM35 Temperature Sensor [package="TO92 [THT]"]
  DC_Power1 = DC Power [voltage=5]
  part_14 = Resistor [tolerance=±5% resistance=10k package=THT]

nets:
  GND: Arduino1.GND, part_12.cathode, LED2.cathode, LED3.cathode, LED4.cathode, LED5.cathode, LED6.cathode, LED7.cathode, LED8.cathode, LED9.cathode, LED10.cathode, LED11.cathode, part_13.GND, DC_Power1.GND, part_14.Pin_1
  N1: Arduino1.D11, part_5.Pin_1
  N2: Arduino1.D10, part_4.Pin_1
  N3: Arduino1.D9, part_6.Pin_1
  N4: Arduino1.D8, part_8.Pin_1
  N5: Arduino1.D7, part_3.Pin_1
  N6: Arduino1.D6, part_7.Pin_1
  N7: Arduino1.D5, part_11.Pin_1
  N8: Arduino1.D4, part_9.Pin_1
  N9: Arduino1.D3, part_13.Vout
  N10: Arduino1.D2, part_2.Pin_1
  N11: Arduino1.D1TX, part_10.Pin_1
  N12: Arduino1.D0RX, part.Pin_1
  N13: Arduino1.+5V, part_13.+Vs, part_14.Pin_0
  N14: Arduino1.VIN, DC_Power1.V+
  N15: part.Pin_0, LED11.anode
  N16: part_2.Pin_0, LED2.anode
  N17: part_3.Pin_0, LED8.anode
  N18: part_4.Pin_0, LED4.anode
  N19: part_5.Pin_0, LED10.anode
  N20: part_6.Pin_0, LED5.anode
  N21: part_7.Pin_0, LED7.anode
  N22: part_8.Pin_0, LED9.anode
  N23: part_9.Pin_0, LED3.anode
  N24: part_10.Pin_0, LED6.anode
  N25: part_11.Pin_0, part_12.anode

custom parts:
  LM35 Temperature Sensor: A LM35 temperature sensor with a temperature range from -55°C to 150°C.
